// Logisim project 16bitcomputer.circ as structural Verilog: 4 circuits, main circuit main
module main (
  input  Carry_In,
  input  [15:0] Bit16_A,
  input  [15:0] Bit16_B,
  output [15:0] Bit16_Result
);

  wire and_1_out, and_2_out, and_3_out, and_4_out, and_5_out, and_6_out, and_7_out, and_8_out, and_9_out,
       and_10_out, and_11_out, and_12_out, and_13_out, and_14_out, and_15_out, and_16_out, and_17_out,
       and_18_out, and_19_out, and_20_out, and_21_out, and_22_out, and_23_out, and_24_out, and_25_out,
       and_26_out, and_27_out, and_28_out, and_29_out, and_30_out, and_31_out, and_32_out, or_1_out,
       or_2_out, or_3_out, or_4_out, or_5_out, or_6_out, or_7_out, or_8_out, or_9_out, or_10_out, or_11_out,
       or_12_out, or_13_out, or_14_out, or_15_out, or_16_out, xor_1_out, xor_2_out, xor_3_out, xor_4_out,
       xor_5_out, xor_6_out, xor_7_out, xor_8_out, xor_9_out, xor_10_out, xor_11_out, xor_12_out, xor_13_out,
       xor_14_out, xor_15_out, xor_16_out;

  and and_1 (and_1_out, Bit16_A[0], Bit16_B[0]);
  and and_2 (and_2_out, Bit16_A[1], Bit16_B[1]);
  and and_3 (and_3_out, Bit16_A[2], Bit16_B[2]);
  and and_4 (and_4_out, Bit16_A[3], Bit16_B[3]);
  and and_5 (and_5_out, Bit16_A[4], Bit16_B[4]);
  and and_6 (and_6_out, Bit16_A[5], Bit16_B[5]);
  and and_7 (and_7_out, Bit16_A[6], Bit16_B[6]);
  and and_8 (and_8_out, Bit16_A[7], Bit16_B[7]);
  and and_9 (and_9_out, Bit16_A[8], Bit16_B[8]);
  and and_10 (and_10_out, Bit16_A[9], Bit16_B[9]);
  and and_11 (and_11_out, Bit16_A[10], Bit16_B[10]);
  and and_12 (and_12_out, Bit16_A[11], Bit16_B[11]);
  and and_13 (and_13_out, Bit16_A[12], Bit16_B[12]);
  and and_14 (and_14_out, Bit16_A[13], Bit16_B[13]);
  and and_15 (and_15_out, Bit16_A[14], Bit16_B[14]);
  and and_16 (and_16_out, Bit16_A[15], Bit16_B[15]);
  xor xor_1 (xor_1_out, Bit16_B[0], Bit16_A[0]);
  xor xor_2 (xor_2_out, Bit16_B[1], Bit16_A[1]);
  xor xor_3 (xor_3_out, Bit16_B[2], Bit16_A[2]);
  xor xor_4 (xor_4_out, Bit16_B[3], Bit16_A[3]);
  xor xor_5 (xor_5_out, Bit16_B[4], Bit16_A[4]);
  xor xor_6 (xor_6_out, Bit16_B[5], Bit16_A[5]);
  xor xor_7 (xor_7_out, Bit16_B[6], Bit16_A[6]);
  xor xor_8 (xor_8_out, Bit16_B[7], Bit16_A[7]);
  xor xor_9 (xor_9_out, Bit16_B[8], Bit16_A[8]);
  xor xor_10 (xor_10_out, Bit16_B[9], Bit16_A[9]);
  xor xor_11 (xor_11_out, Bit16_B[10], Bit16_A[10]);
  xor xor_12 (xor_12_out, Bit16_B[11], Bit16_A[11]);
  xor xor_13 (xor_13_out, Bit16_B[12], Bit16_A[12]);
  xor xor_14 (xor_14_out, Bit16_B[13], Bit16_A[13]);
  xor xor_15 (xor_15_out, Bit16_B[14], Bit16_A[14]);
  xor xor_16 (xor_16_out, Bit16_B[15], Bit16_A[15]);
  and and_17 (and_17_out, Carry_In, xor_1_out);
  and and_18 (and_18_out, or_1_out, xor_2_out);
  and and_19 (and_19_out, or_2_out, xor_3_out);
  and and_20 (and_20_out, or_3_out, xor_4_out);
  and and_21 (and_21_out, or_4_out, xor_5_out);
  and and_22 (and_22_out, or_5_out, xor_6_out);
  and and_23 (and_23_out, or_6_out, xor_7_out);
  and and_24 (and_24_out, or_7_out, xor_8_out);
  and and_25 (and_25_out, or_8_out, xor_9_out);
  and and_26 (and_26_out, or_9_out, xor_10_out);
  and and_27 (and_27_out, or_10_out, xor_11_out);
  and and_28 (and_28_out, or_11_out, xor_12_out);
  and and_29 (and_29_out, or_12_out, xor_13_out);
  and and_30 (and_30_out, or_13_out, xor_14_out);
  and and_31 (and_31_out, or_14_out, xor_15_out);
  and and_32 (and_32_out, or_15_out, xor_16_out);
  xor xor_17 (Bit16_Result[0], Carry_In, xor_1_out);
  xor xor_18 (Bit16_Result[1], or_1_out, xor_2_out);
  xor xor_19 (Bit16_Result[2], or_2_out, xor_3_out);
  xor xor_20 (Bit16_Result[3], or_3_out, xor_4_out);
  xor xor_21 (Bit16_Result[4], or_4_out, xor_5_out);
  xor xor_22 (Bit16_Result[5], or_5_out, xor_6_out);
  xor xor_23 (Bit16_Result[6], or_6_out, xor_7_out);
  xor xor_24 (Bit16_Result[7], or_7_out, xor_8_out);
  xor xor_25 (Bit16_Result[8], or_8_out, xor_9_out);
  xor xor_26 (Bit16_Result[9], or_9_out, xor_10_out);
  xor xor_27 (Bit16_Result[10], or_10_out, xor_11_out);
  xor xor_28 (Bit16_Result[11], or_11_out, xor_12_out);
  xor xor_29 (Bit16_Result[12], or_12_out, xor_13_out);
  xor xor_30 (Bit16_Result[13], or_13_out, xor_14_out);
  xor xor_31 (Bit16_Result[14], or_14_out, xor_15_out);
  xor xor_32 (Bit16_Result[15], or_15_out, xor_16_out);
  or or_1 (or_1_out, and_17_out, and_1_out);
  or or_2 (or_2_out, and_18_out, and_2_out);
  or or_3 (or_3_out, and_19_out, and_3_out);
  or or_4 (or_4_out, and_20_out, and_4_out);
  or or_5 (or_5_out, and_21_out, and_5_out);
  or or_6 (or_6_out, and_22_out, and_6_out);
  or or_7 (or_7_out, and_23_out, and_7_out);
  or or_8 (or_8_out, and_24_out, and_8_out);
  or or_9 (or_9_out, and_25_out, and_9_out);
  or or_10 (or_10_out, and_26_out, and_10_out);
  or or_11 (or_11_out, and_27_out, and_11_out);
  or or_12 (or_12_out, and_28_out, and_12_out);
  or or_13 (or_13_out, and_29_out, and_13_out);
  or or_14 (or_14_out, and_30_out, and_14_out);
  or or_15 (or_15_out, and_31_out, and_15_out);
  or or_16 (or_16_out, and_32_out, and_16_out);
endmodule

module Bit16_Add (
  input  Carry_In,
  input  [15:0] Bit16_A,
  input  [15:0] Bit16_B,
  output [15:0] Bit16_Result
);

  wire and_1_out, and_2_out, and_3_out, and_4_out, and_5_out, and_6_out, and_7_out, and_8_out, and_9_out,
       and_10_out, and_11_out, and_12_out, and_13_out, and_14_out, and_15_out, and_16_out, and_17_out,
       and_18_out, and_19_out, and_20_out, and_21_out, and_22_out, and_23_out, and_24_out, and_25_out,
       and_26_out, and_27_out, and_28_out, and_29_out, and_30_out, and_31_out, and_32_out, or_1_out,
       or_2_out, or_3_out, or_4_out, or_5_out, or_6_out, or_7_out, or_8_out, or_9_out, or_10_out, or_11_out,
       or_12_out, or_13_out, or_14_out, or_15_out, or_16_out, xor_1_out, xor_2_out, xor_3_out, xor_4_out,
       xor_5_out, xor_6_out, xor_7_out, xor_8_out, xor_9_out, xor_10_out, xor_11_out, xor_12_out, xor_13_out,
       xor_14_out, xor_15_out, xor_16_out;

  and and_1 (and_1_out, Bit16_A[0], Bit16_B[0]);
  and and_2 (and_2_out, Bit16_A[1], Bit16_B[1]);
  and and_3 (and_3_out, Bit16_A[2], Bit16_B[2]);
  and and_4 (and_4_out, Bit16_A[3], Bit16_B[3]);
  and and_5 (and_5_out, Bit16_A[4], Bit16_B[4]);
  and and_6 (and_6_out, Bit16_A[5], Bit16_B[5]);
  and and_7 (and_7_out, Bit16_A[6], Bit16_B[6]);
  and and_8 (and_8_out, Bit16_A[7], Bit16_B[7]);
  and and_9 (and_9_out, Bit16_A[8], Bit16_B[8]);
  and and_10 (and_10_out, Bit16_A[9], Bit16_B[9]);
  and and_11 (and_11_out, Bit16_A[10], Bit16_B[10]);
  and and_12 (and_12_out, Bit16_A[11], Bit16_B[11]);
  and and_13 (and_13_out, Bit16_A[12], Bit16_B[12]);
  and and_14 (and_14_out, Bit16_A[13], Bit16_B[13]);
  and and_15 (and_15_out, Bit16_A[14], Bit16_B[14]);
  and and_16 (and_16_out, Bit16_A[15], Bit16_B[15]);
  xor xor_1 (xor_1_out, Bit16_B[0], Bit16_A[0]);
  xor xor_2 (xor_2_out, Bit16_B[1], Bit16_A[1]);
  xor xor_3 (xor_3_out, Bit16_B[2], Bit16_A[2]);
  xor xor_4 (xor_4_out, Bit16_B[3], Bit16_A[3]);
  xor xor_5 (xor_5_out, Bit16_B[4], Bit16_A[4]);
  xor xor_6 (xor_6_out, Bit16_B[5], Bit16_A[5]);
  xor xor_7 (xor_7_out, Bit16_B[6], Bit16_A[6]);
  xor xor_8 (xor_8_out, Bit16_B[7], Bit16_A[7]);
  xor xor_9 (xor_9_out, Bit16_B[8], Bit16_A[8]);
  xor xor_10 (xor_10_out, Bit16_B[9], Bit16_A[9]);
  xor xor_11 (xor_11_out, Bit16_B[10], Bit16_A[10]);
  xor xor_12 (xor_12_out, Bit16_B[11], Bit16_A[11]);
  xor xor_13 (xor_13_out, Bit16_B[12], Bit16_A[12]);
  xor xor_14 (xor_14_out, Bit16_B[13], Bit16_A[13]);
  xor xor_15 (xor_15_out, Bit16_B[14], Bit16_A[14]);
  xor xor_16 (xor_16_out, Bit16_B[15], Bit16_A[15]);
  and and_17 (and_17_out, Carry_In, xor_1_out);
  and and_18 (and_18_out, or_1_out, xor_2_out);
  and and_19 (and_19_out, or_2_out, xor_3_out);
  and and_20 (and_20_out, or_3_out, xor_4_out);
  and and_21 (and_21_out, or_4_out, xor_5_out);
  and and_22 (and_22_out, or_5_out, xor_6_out);
  and and_23 (and_23_out, or_6_out, xor_7_out);
  and and_24 (and_24_out, or_7_out, xor_8_out);
  and and_25 (and_25_out, or_8_out, xor_9_out);
  and and_26 (and_26_out, or_9_out, xor_10_out);
  and and_27 (and_27_out, or_10_out, xor_11_out);
  and and_28 (and_28_out, or_11_out, xor_12_out);
  and and_29 (and_29_out, or_12_out, xor_13_out);
  and and_30 (and_30_out, or_13_out, xor_14_out);
  and and_31 (and_31_out, or_14_out, xor_15_out);
  and and_32 (and_32_out, or_15_out, xor_16_out);
  xor xor_17 (Bit16_Result[0], Carry_In, xor_1_out);
  xor xor_18 (Bit16_Result[1], or_1_out, xor_2_out);
  xor xor_19 (Bit16_Result[2], or_2_out, xor_3_out);
  xor xor_20 (Bit16_Result[3], or_3_out, xor_4_out);
  xor xor_21 (Bit16_Result[4], or_4_out, xor_5_out);
  xor xor_22 (Bit16_Result[5], or_5_out, xor_6_out);
  xor xor_23 (Bit16_Result[6], or_6_out, xor_7_out);
  xor xor_24 (Bit16_Result[7], or_7_out, xor_8_out);
  xor xor_25 (Bit16_Result[8], or_8_out, xor_9_out);
  xor xor_26 (Bit16_Result[9], or_9_out, xor_10_out);
  xor xor_27 (Bit16_Result[10], or_10_out, xor_11_out);
  xor xor_28 (Bit16_Result[11], or_11_out, xor_12_out);
  xor xor_29 (Bit16_Result[12], or_12_out, xor_13_out);
  xor xor_30 (Bit16_Result[13], or_13_out, xor_14_out);
  xor xor_31 (Bit16_Result[14], or_14_out, xor_15_out);
  xor xor_32 (Bit16_Result[15], or_15_out, xor_16_out);
  or or_1 (or_1_out, and_17_out, and_1_out);
  or or_2 (or_2_out, and_18_out, and_2_out);
  or or_3 (or_3_out, and_19_out, and_3_out);
  or or_4 (or_4_out, and_20_out, and_4_out);
  or or_5 (or_5_out, and_21_out, and_5_out);
  or or_6 (or_6_out, and_22_out, and_6_out);
  or or_7 (or_7_out, and_23_out, and_7_out);
  or or_8 (or_8_out, and_24_out, and_8_out);
  or or_9 (or_9_out, and_25_out, and_9_out);
  or or_10 (or_10_out, and_26_out, and_10_out);
  or or_11 (or_11_out, and_27_out, and_11_out);
  or or_12 (or_12_out, and_28_out, and_12_out);
  or or_13 (or_13_out, and_29_out, and_13_out);
  or or_14 (or_14_out, and_30_out, and_14_out);
  or or_15 (or_15_out, and_31_out, and_15_out);
  or or_16 (or_16_out, and_32_out, and_16_out);
endmodule

module Bit16_ALU (
);

  wire [15:0] twos_complementer_1_bit16_result, twos_complementer_2_bit16_result;

  Twos_Complementer twos_complementer_1 (.Bit16_Result(twos_complementer_1_bit16_result));  // open: Allow_Twos_Complement, Bit16_Input
  Twos_Complementer twos_complementer_2 (.Bit16_Result(twos_complementer_2_bit16_result));  // open: Allow_Twos_Complement, Bit16_Input
  Bit16_Add bit16_add_1 (
    .Bit16_A(twos_complementer_1_bit16_result), .Bit16_B(twos_complementer_2_bit16_result));  // open: Carry_In, Bit16_Result
endmodule

module Twos_Complementer (
  input  Allow_Twos_Complement,
  input  [15:0] Bit16_Input,
  output [15:0] Bit16_Result
);

  wire and_1_out, and_2_out, and_3_out, and_4_out, and_5_out, and_6_out, and_7_out, and_8_out, and_9_out,
       and_10_out, and_11_out, and_12_out, and_13_out, and_14_out, and_15_out, or_1_out, or_2_out, or_3_out,
       or_4_out, or_5_out, or_6_out, or_7_out, or_8_out, or_9_out, or_10_out, or_11_out, or_12_out,
       or_13_out, or_14_out;

  and and_1 (and_1_out, Bit16_Input[0], Allow_Twos_Complement);
  and and_2 (and_2_out, Bit16_Result[1], Allow_Twos_Complement);
  or or_1 (or_1_out, and_1_out, and_2_out);
  and and_3 (and_3_out, Bit16_Result[2], Allow_Twos_Complement);
  or or_2 (or_2_out, and_1_out, and_2_out, and_3_out);
  and and_4 (and_4_out, Bit16_Result[3], Allow_Twos_Complement);
  or or_3 (or_3_out, and_1_out, and_2_out, and_3_out, and_4_out);
  and and_5 (and_5_out, Bit16_Result[4], Allow_Twos_Complement);
  or or_4 (or_4_out, and_1_out, and_2_out, and_3_out, and_4_out, and_5_out);
  and and_6 (and_6_out, Bit16_Result[5], Allow_Twos_Complement);
  or or_5 (or_5_out, and_1_out, and_2_out, and_3_out, and_4_out, and_5_out, and_6_out);
  and and_7 (and_7_out, Bit16_Result[6], Allow_Twos_Complement);
  or or_6 (or_6_out, and_1_out, and_2_out, and_3_out, and_4_out, and_5_out, and_6_out, and_7_out);
  and and_8 (and_8_out, Bit16_Result[7], Allow_Twos_Complement);
  or or_7 (or_7_out, and_1_out, and_2_out, and_3_out, and_4_out, and_5_out, and_6_out, and_7_out, and_8_out);
  and and_9 (and_9_out, Bit16_Result[8], Allow_Twos_Complement);
  or or_8 (or_8_out, and_1_out, and_2_out, and_3_out, and_4_out, and_5_out, and_6_out, and_7_out, and_8_out, and_9_out);
  and and_10 (and_10_out, Bit16_Result[9], Allow_Twos_Complement);
  or or_9 (or_9_out, and_1_out, and_2_out, and_3_out, and_4_out, and_5_out, and_6_out, and_7_out, and_8_out, and_9_out, and_10_out);
  and and_11 (and_11_out, Bit16_Result[10], Allow_Twos_Complement);
  or or_10 (or_10_out, and_1_out, and_2_out, and_3_out, and_4_out, and_5_out, and_6_out, and_7_out, and_8_out, and_9_out, and_10_out, and_11_out);
  and and_12 (and_12_out, Bit16_Result[11], Allow_Twos_Complement);
  or or_11 (or_11_out, and_1_out, and_2_out, and_3_out, and_4_out, and_5_out, and_6_out, and_7_out, and_8_out, and_9_out, and_10_out, and_11_out, and_12_out);
  and and_13 (and_13_out, Bit16_Result[12], Allow_Twos_Complement);
  or or_12 (or_12_out, and_1_out, and_2_out, and_3_out, and_4_out, and_5_out, and_6_out, and_7_out, and_8_out, and_9_out, and_10_out, and_11_out, and_12_out, and_13_out);
  and and_14 (and_14_out, Bit16_Result[13], Allow_Twos_Complement);
  or or_13 (or_13_out, and_1_out, and_2_out, and_3_out, and_4_out, and_5_out, and_6_out, and_7_out, and_8_out, and_9_out, and_10_out, and_11_out, and_12_out, and_13_out, and_14_out);
  and and_15 (and_15_out, Bit16_Result[14], Allow_Twos_Complement);
  or or_14 (or_14_out, and_1_out, and_2_out, and_3_out, and_4_out, and_5_out, and_6_out, and_7_out, and_8_out, and_9_out, and_10_out, and_11_out, and_12_out, and_13_out, and_14_out, and_15_out);
  xor xor_1 (Bit16_Result[1], and_1_out, Bit16_Input[1]);
  xor xor_2 (Bit16_Result[2], or_1_out, Bit16_Input[2]);
  xor xor_3 (Bit16_Result[3], or_2_out, Bit16_Input[3]);
  xor xor_4 (Bit16_Result[4], or_3_out, Bit16_Input[4]);
  xor xor_5 (Bit16_Result[5], or_4_out, Bit16_Input[5]);
  xor xor_6 (Bit16_Result[6], or_5_out, Bit16_Input[6]);
  xor xor_7 (Bit16_Result[7], or_6_out, Bit16_Input[7]);
  xor xor_8 (Bit16_Result[8], or_7_out, Bit16_Input[8]);
  xor xor_9 (Bit16_Result[9], or_8_out, Bit16_Input[9]);
  xor xor_10 (Bit16_Result[10], or_9_out, Bit16_Input[10]);
  xor xor_11 (Bit16_Result[11], or_10_out, Bit16_Input[11]);
  xor xor_12 (Bit16_Result[12], or_11_out, Bit16_Input[12]);
  xor xor_13 (Bit16_Result[13], or_12_out, Bit16_Input[13]);
  xor xor_14 (Bit16_Result[14], or_13_out, Bit16_Input[14]);
  xor xor_15 (Bit16_Result[15], or_14_out, Bit16_Input[15]);

  assign Bit16_Result[0] = Bit16_Input[0];
endmodule
